// Logisim project projet.circ as structural Verilog
module add (
  input  [3:0] in_1,
  input  in_2,
  input  in_3,
  input  [4:0] in_4,
  input  [4:0] in_5,
  input  [4:0] in_6,
  input  in_7
);

  wire registerfile_1_p8, registerfile_1_p9;
  wire [3:0] registerfile_1_p1, registerfile_1_p1_2, registerfile_1_p1_3, registerfile_1_p1_4,
       registerfile_1_p1_5, registerfile_1_p1_7;
  wire [31:20] registerfile_1_p1_6;

  // RegisterFile registerfile_1: pin names not known; wires that end beside it: {registerfile_1_p1_6[31:28], registerfile_1_p1_7, registerfile_1_p1_6[23:20], registerfile_1_p1_5, registerfile_1_p1_4, registerfile_1_p1_3, registerfile_1_p1_2, registerfile_1_p1}, in_2, in_3, in_4, in_5, in_6, in_7, registerfile_1_p8, registerfile_1_p9
  // MIPS_ALU mips_alu_1: pin names not known; wires that end beside it: registerfile_1_p8, registerfile_1_p9, in_1, {registerfile_1_p1_6[31:28], registerfile_1_p1_7, registerfile_1_p1_6[23:20], registerfile_1_p1_5, registerfile_1_p1_4, registerfile_1_p1_3, registerfile_1_p1_2, registerfile_1_p1}
  Hex_Digit_Display hex_digit_display_1 (.value(registerfile_1_p1_6[31:28]));  // open: dp
  Hex_Digit_Display hex_digit_display_2 (.value(registerfile_1_p1_7));  // open: dp
  Hex_Digit_Display hex_digit_display_3 (.value(registerfile_1_p1_6[23:20]));  // open: dp
  Hex_Digit_Display hex_digit_display_4 (.value(registerfile_1_p1_4));  // open: dp
  Hex_Digit_Display hex_digit_display_5 (.value(registerfile_1_p1_5));  // open: dp
  Hex_Digit_Display hex_digit_display_6 (.value(registerfile_1_p1_3));  // open: dp
  Hex_Digit_Display hex_digit_display_7 (.value(registerfile_1_p1_2));  // open: dp
  Hex_Digit_Display hex_digit_display_8 (.value(registerfile_1_p1));  // open: dp
endmodule

module addi (
  input  [4:0] in_1,
  input  [4:0] in_2,
  input  [4:0] in_3,
  input  [31:0] in_4,
  input  [31:0] ImmS,
  input  [3:0] in_6,
  input  mx1,
  input  in_8,
  input  in_9,
  input  in_10,
  input  in_11
);

  wire registerfile_1_p8;
  wire [3:0] registerfile_1_p1, registerfile_1_p1_2, registerfile_1_p1_4;
  wire [4:0] registerfile_1_p4;
  wire [31:0] multiplexer_2_out, registerfile_1_p9;
  wire [31:8] registerfile_1_p1_3;

  // RegisterFile registerfile_1: pin names not known; wires that end beside it: {registerfile_1_p1_3[31:20], registerfile_1_p1_4, registerfile_1_p1_3[15:8], registerfile_1_p1_2, registerfile_1_p1}, in_8, in_9, registerfile_1_p4, in_2, in_1, in_10, registerfile_1_p8, registerfile_1_p9
  Multiplexer #(.width(5)) multiplexer_1 (.in0(in_1), .in1(in_3), .out(registerfile_1_p4), .sel(in_11));  // open: en
  Multiplexer #(.width(32)) multiplexer_2 (
    .in0(ImmS), .in1(registerfile_1_p9), .out(multiplexer_2_out), .sel(mx1));  // open: en
  // MIPS_ALU mips_alu_1: pin names not known; wires that end beside it: registerfile_1_p8, multiplexer_2_out, in_6, {registerfile_1_p1_3[31:20], registerfile_1_p1_4, registerfile_1_p1_3[15:8], registerfile_1_p1_2, registerfile_1_p1}
  Hex_Digit_Display hex_digit_display_1 (.value(registerfile_1_p1_3[31:28]));  // open: dp
  Hex_Digit_Display hex_digit_display_2 (.value(registerfile_1_p1_3[27:24]));  // open: dp
  Hex_Digit_Display hex_digit_display_3 (.value(registerfile_1_p1_4));  // open: dp
  Hex_Digit_Display hex_digit_display_4 (.value(registerfile_1_p1_3[23:20]));  // open: dp
  Hex_Digit_Display hex_digit_display_5 (.value(registerfile_1_p1_3[15:12]));  // open: dp
  Hex_Digit_Display hex_digit_display_6 (.value(registerfile_1_p1_3[11:8]));  // open: dp
  Hex_Digit_Display hex_digit_display_7 (.value(registerfile_1_p1_2));  // open: dp
  Hex_Digit_Display hex_digit_display_8 (.value(registerfile_1_p1));  // open: dp

  // Other names for the same wires on the sheet: ImmS_t[31:0] = in_4; rd[4:0] = in_3; rs[4:0] = in_2; rt[4:0] = in_1
endmodule

module \and  (
  input  [4:0] in_1,
  input  [4:0] in_2,
  input  [4:0] in_3,
  input  [31:0] in_4,
  input  [31:0] ImmS,
  input  [3:0] in_6,
  input  mx1,
  input  in_8,
  input  in_9,
  input  in_10,
  input  in_11
);

  wire registerfile_1_p8;
  wire [3:0] registerfile_1_p1, registerfile_1_p1_2, registerfile_1_p1_4;
  wire [4:0] registerfile_1_p4;
  wire [31:0] multiplexer_2_out, registerfile_1_p9;
  wire [31:8] registerfile_1_p1_3;

  // RegisterFile registerfile_1: pin names not known; wires that end beside it: {registerfile_1_p1_3[31:20], registerfile_1_p1_4, registerfile_1_p1_3[15:8], registerfile_1_p1_2, registerfile_1_p1}, in_8, in_9, registerfile_1_p4, in_2, in_1, in_10, registerfile_1_p8, registerfile_1_p9
  Multiplexer #(.width(5)) multiplexer_1 (.in0(in_1), .in1(in_3), .out(registerfile_1_p4), .sel(in_11));  // open: en
  Multiplexer #(.width(32)) multiplexer_2 (
    .in0(ImmS), .in1(registerfile_1_p9), .out(multiplexer_2_out), .sel(mx1));  // open: en
  // MIPS_ALU mips_alu_1: pin names not known; wires that end beside it: registerfile_1_p8, multiplexer_2_out, in_6, {registerfile_1_p1_3[31:20], registerfile_1_p1_4, registerfile_1_p1_3[15:8], registerfile_1_p1_2, registerfile_1_p1}
  Hex_Digit_Display hex_digit_display_1 (.value(registerfile_1_p1_3[31:28]));  // open: dp
  Hex_Digit_Display hex_digit_display_2 (.value(registerfile_1_p1_3[27:24]));  // open: dp
  Hex_Digit_Display hex_digit_display_3 (.value(registerfile_1_p1_4));  // open: dp
  Hex_Digit_Display hex_digit_display_4 (.value(registerfile_1_p1_3[23:20]));  // open: dp
  Hex_Digit_Display hex_digit_display_5 (.value(registerfile_1_p1_3[15:12]));  // open: dp
  Hex_Digit_Display hex_digit_display_6 (.value(registerfile_1_p1_3[11:8]));  // open: dp
  Hex_Digit_Display hex_digit_display_7 (.value(registerfile_1_p1_2));  // open: dp
  Hex_Digit_Display hex_digit_display_8 (.value(registerfile_1_p1));  // open: dp

  // Other names for the same wires on the sheet: ImmS_t[31:0] = in_4; rd[4:0] = in_3; rs[4:0] = in_2; rt[4:0] = in_1
endmodule
